// Digital circuit Circuit_De_Controle.dig as structural Verilog
module Circuit_De_Controle (
  input  B0,
  input  Fin,
  input  Clk,
  output Raz,
  output Wop,
  output Wres,
  output Dec,
  output D1,
  output D0
);

  wire and_1_out, and_2_out, and_4_out, and_5_out, and_7_out, and_9_out, and_10_out, and_11_out, D0_nq,
       D1_nq, not_1_out, or_1_out, or_2_out, or_3_out, or_4_out;

  D_FF u_D1 (.D(or_2_out), .C(Clk), .Q(D1), .nQ(D1_nq));
  and and_1 (and_1_out, D0_nq, or_1_out);
  or or_1 (or_1_out, not_1_out, and_2_out);
  or or_2 (or_2_out, and_1_out, and_5_out);
  and and_2 (and_2_out, Fin, D1);
  and and_3 (Raz, D0_nq, D1_nq);
  and and_4 (and_4_out, D0_nq, Clk);
  Delay #(.delayTime(3)) delay_1 (.in(and_4_out), .out(Wop));
  and and_5 (and_5_out, D1_nq, or_3_out);
  or or_3 (or_3_out, not_1_out, D0);
  not not_1 (not_1_out, B0);
  and and_6 (Wres, D0, D1_nq);
  and and_7 (and_7_out, D0_nq, D1);
  and and_8 (Dec, and_7_out, Clk);
  D_FF u_D0 (.D(and_10_out), .C(Clk), .Q(D0), .nQ(D0_nq));
  and and_9 (and_9_out, B0, 1'b1);
  or or_4 (or_4_out, and_9_out, and_11_out);
  and and_10 (and_10_out, or_4_out, D0_nq);
  and and_11 (and_11_out, D1, Fin);
endmodule
