// Digital circuit UAL.dig as structural Verilog
module UAL (
  input  sub
);

  wire [31:0] add_1_s, barrelshifter_1_out, barrelshifter_2_out, comparator_1_lt, comparator_2_lt, undriven,
       undriven_2, xor_1_out, xor_2_out;

  xor xor_1 (xor_1_out[0], undriven_2[0], sub);
  Add #(.Bits(32)) add_1 (.a(undriven), .b(xor_1_out), .c_i(sub), .s(add_1_s));  // open: c_o
  BarrelShifter #(.Bits(32)) barrelshifter_1 (.in(undriven), .shift(undriven_2[4:0]), .out(barrelshifter_1_out));
  Comparator comparator_1 (.a(undriven[0]), .b(sub), .lt(comparator_1_lt[0]));  // open: gt, eq
  Comparator comparator_2 (.a(undriven[0]), .b(sub), .lt(comparator_2_lt[0]));  // open: gt, eq
  assign xor_2_out = undriven ^ {32{sub}};  // XOr xor_2, 32 bits wide
  BarrelShifter #(.Bits(32)) barrelshifter_2 (.in(undriven), .shift({32{sub}}), .out(barrelshifter_2_out));
  // Or or_1 is placed but not wired
  Multiplexer #(.Bits(32), .Selector_Bits(3)) multiplexer_1 (
    .in_0(add_1_s), .in_1(barrelshifter_1_out), .in_2(comparator_1_lt), .in_3(comparator_2_lt),
    .in_4(xor_2_out), .in_5(barrelshifter_2_out));  // open: sel, in_6, in_7, out
  // Pins of 1 and 32 bits meet at undriven
  // Pins of 1 and 32 bits meet at xor_1_out
  // Pins of 1 and 32 bits meet at comparator_1_lt
  // Pins of 1 and 32 bits meet at comparator_2_lt
  // Pins of 1 and 32 bits meet at undriven_2
  // Pins of 1 and 32 bits meet at {32{sub}}
endmodule
